# Fritzing sketch Leonardo-with-button (saved by Fritzing 0.9.0b)
breadboards: 1

parts:
  Composant1 = Arduino Leonardo (Rev3b)
  S1 = Pushbutton [package="[THT]"]
  R2 = Resistor [tolerance=±5% resistance=10k package=THT]

nets:
  N1: Composant1.D2/SDA, S1.Pin_3, S1.Pin_4, R2.Pin_0
  N2: Composant1.5V, S1.Pin_1, S1.Pin_2
  N3: Composant1.GND, R2.Pin_1
