# Fritzing sketch Leonardo-with-lcd (saved by Fritzing 0.9.0b)
breadboards: 1

parts:
  Composant1 = Arduino Leonardo (Rev3b)
  U1 = LCD-16X2 [package=lcd-16x2]
  R3 = Resistor [tolerance=±5% resistance=220 package=THT]

nets:
  N1: Composant1.D2/SDA, U1.DB7
  N2: Composant1.D3_PWM/SCL, U1.DB6
  N3: Composant1.D4/A6, U1.DB5
  N4: Composant1.D5_PWM, U1.DB4
  5V: Composant1.5V, U1.VDD
  GND: Composant1.GND, U1.VSS, U1.VO, U1.R_W, U1.K, R3.Pin_1
  N5: Composant1.D11_PWM, U1.E
  N6: Composant1.D12/A11, U1.RS
  N7: U1.A, R3.Pin_0
