# Fritzing sketch Teensy3-with-LCD (saved by Fritzing 0.9.0b)
breadboards: 1

parts:
  Teensy_3_1 = Teensy 3.0
  U1 = LCD-16X2 [package=lcd-16x2]
  X1 = USB Connectors [package=usb-a-s-nosilk]
  R1 = Resistor [tolerance=±5% resistance=220 package=THT]
  R2 = Resistor [tolerance=±5% resistance=1k package=THT]
  R3 = Resistor [tolerance=±5% resistance=1k package=THT]
  R4 = Resistor [tolerance=±5% resistance=1k package=THT]
  R5 = Resistor [tolerance=±5% resistance=1k package=THT]

nets:
  GND: Teensy_3_1.GND, U1.VSS, U1.VO, U1.R_W, U1.K, X1.GND
  N1: Teensy_3_1.D2, R2.Pin_1
  N2: Teensy_3_1.D3, R3.Pin_1
  N3: Teensy_3_1.D4, R4.Pin_1
  N4: Teensy_3_1.D5, R5.Pin_1
  N5: Teensy_3_1.A1/D15, U1.RS
  N6: Teensy_3_1.A2/D16, U1.E
  N7: U1.VDD, X1.VBUS, R1.Pin_1
  N8: U1.DB4, R5.Pin_0
  N9: U1.DB5, R4.Pin_0
  N10: U1.DB6, R3.Pin_0
  N11: U1.DB7, R2.Pin_0
  N12: U1.A, R1.Pin_0
